// Logisim project alu.circ as structural Verilog: 3 circuits, main circuit ALU
module ALU (
  input  [31:0] in_1,
  input  [31:0] in_2,
  input  [3:0] in_3,
  output [31:0] out_4
);

  wire [31:0] adder_1_out, and_1_out, or_1_out, subtractor_1_out;

  Adder #(.width(32)) adder_1 (.a(in_1), .b(in_2), .out(adder_1_out));  // open: cin, cout
  Subtractor #(.width(32)) subtractor_1 (.a(in_1), .b(in_2), .out(subtractor_1_out));  // open: bin, bout
  assign and_1_out = in_1 & in_2;  // AND_Gate and_1, 32 bits wide
  assign or_1_out = in_1 | in_2;  // OR_Gate or_1, 32 bits wide
  Multiplexer #(.select(4), .width(32), .enable("false")) multiplexer_1 (
    .in0(adder_1_out), .in1(subtractor_1_out), .in2(and_1_out), .in3(or_1_out), .out(out_4), .sel(in_3));  // open: in4, in5, in6, in7, in8, in9, in10, in11, in12, in13, in14, in15

  // Other names for the same wires on the sheet: Input_A[31:0] = in_1; Input_B[31:0] = in_2
endmodule

module ALU_Control_Logic (
  input  [5:0] Operacion_R,
  input  [5:0] Opcode,
  input  ALU_OP,
  output [3:0] out_4
);

  wire comparator_1_eq;
  wire [5:0] multiplexer_1_out;

  Comparator #(.width(6)) comparator_1 (.a(Opcode), .b({6{1'b0}}), .eq(comparator_1_eq));  // open: gt, lt
  Multiplexer #(.width(6), .disabled(0)) multiplexer_1 (
    .in0(Opcode), .in1(Operacion_R), .out(multiplexer_1_out), .sel(comparator_1_eq), .en(ALU_OP));
  Interprete_Operacion interprete_operacion_1 (.Operation(multiplexer_1_out), .ALU_OP(out_4));
endmodule

module Interprete_Operacion (
  input  [5:0] Operation,
  output [3:0] ALU_OP
);

  wire and_1_out, and_2_out, and_3_out, and_4_out, and_5_out, and_6_out, and_7_out, and_8_out, and_9_out,
       not_1_out, not_2_out, not_3_out, not_4_out, not_5_out, not_6_out, not_7_out, not_8_out, not_9_out,
       not_10_out, not_11_out, not_12_out, not_13_out, not_14_out, not_15_out, not_16_out, not_17_out,
       not_18_out, not_19_out, not_20_out, not_21_out, not_22_out, not_23_out, not_24_out, not_25_out,
       not_26_out, not_27_out, not_28_out, not_29_out, not_30_out, not_31_out, not_32_out, not_33_out;

  not not_1 (not_1_out, Operation[5]);
  not not_2 (not_2_out, Operation[4]);
  not not_3 (not_3_out, Operation[1]);
  not not_4 (not_4_out, Operation[4]);
  not not_5 (not_5_out, Operation[3]);
  not not_6 (not_6_out, Operation[1]);
  not not_7 (not_7_out, Operation[5]);
  not not_8 (not_8_out, Operation[4]);
  not not_9 (not_9_out, Operation[1]);
  not not_10 (not_10_out, Operation[0]);
  not not_11 (not_11_out, Operation[4]);
  not not_12 (not_12_out, Operation[3]);
  not not_13 (not_13_out, Operation[2]);
  not not_14 (not_14_out, Operation[4]);
  not not_15 (not_15_out, Operation[3]);
  not not_16 (not_16_out, Operation[1]);
  not not_17 (not_17_out, Operation[0]);
  not not_18 (not_18_out, Operation[5]);
  not not_19 (not_19_out, Operation[4]);
  not not_20 (not_20_out, Operation[2]);
  not not_21 (not_21_out, Operation[1]);
  not not_22 (not_22_out, Operation[5]);
  not not_23 (not_23_out, Operation[4]);
  not not_24 (not_24_out, Operation[1]);
  not not_25 (not_25_out, Operation[0]);
  not not_26 (not_26_out, Operation[4]);
  not not_27 (not_27_out, Operation[3]);
  not not_28 (not_28_out, Operation[2]);
  not not_29 (not_29_out, Operation[1]);
  not not_30 (not_30_out, Operation[4]);
  not not_31 (not_31_out, Operation[3]);
  not not_32 (not_32_out, Operation[1]);
  not not_33 (not_33_out, Operation[0]);
  and and_1 (and_1_out, not_1_out, not_2_out, Operation[3], Operation[2], not_3_out, Operation[0]);
  and and_2 (and_2_out, Operation[5], not_4_out, not_5_out, Operation[2], not_6_out, Operation[0]);
  and and_3 (and_3_out, not_7_out, not_8_out, Operation[3], Operation[2], not_9_out, not_10_out);
  and and_4 (and_4_out, Operation[5], not_11_out, not_12_out, not_13_out, Operation[1]);
  and and_5 (and_5_out, Operation[5], not_14_out, not_15_out, Operation[2], not_16_out, not_17_out);
  and and_6 (and_6_out, not_18_out, not_19_out, Operation[3], not_20_out, not_21_out);
  and and_7 (and_7_out, not_22_out, not_23_out, Operation[3], not_24_out, not_25_out);
  and and_8 (and_8_out, Operation[5], not_26_out, not_27_out, not_28_out, not_29_out);
  and and_9 (and_9_out, Operation[5], not_30_out, not_31_out, not_32_out, not_33_out);
  or or_1 (ALU_OP[2], and_1_out, and_2_out);
  or or_2 (ALU_OP[1], and_3_out, and_4_out, and_5_out);
  or or_3 (ALU_OP[0], and_6_out, and_7_out, and_8_out, and_9_out);

  assign ALU_OP[3] = 1'b0;
endmodule
