// Logisim project control logic.circ as structural Verilog: 2 circuits, main circuit Unidad de Control
module Unidad_de_Control (
  input  [5:0] Opcode,
  output alu,
  output EscMem,
  output EscReg,
  output LeeMem,
  output Branch
);

  wire not_1_out, not_2_out, not_3_out, not_4_out, not_5_out;

  not not_1 (not_1_out, Opcode[0]);
  not not_2 (not_2_out, Opcode[1]);
  not not_3 (not_3_out, Opcode[3]);
  not not_4 (not_4_out, Opcode[4]);
  not not_5 (not_5_out, Opcode[5]);
  and and_1 (alu, not_1_out, not_2_out, not_3_out, not_4_out, not_5_out);

  assign Branch = 1'b0;
  assign EscMem = 1'b0;
  assign EscReg = 1'b0;
  assign LeeMem = 1'b0;
endmodule

module CU (
  input  I5,
  input  I4,
  input  I3,
  input  I2,
  input  I1,
  input  I0,
  output alu,
  output EscMem,
  output EscReg,
  output LeeMem,
  output Branch
);

  wire not_1_out, not_2_out, not_3_out, not_4_out, not_5_out;

  not not_1 (not_1_out, I5);
  not not_2 (not_2_out, I4);
  not not_3 (not_3_out, I2);
  not not_4 (not_4_out, I1);
  not not_5 (not_5_out, I0);
  and and_1 (alu, not_1_out, not_2_out, not_3_out, not_4_out, not_5_out);

  assign Branch = 1'b0;
  assign EscMem = 1'b0;
  assign EscReg = 1'b0;
  assign LeeMem = 1'b0;
endmodule
