// Logisim project inst logic.circ as structural Verilog
module Parser_de_Inst (
  input  [31:0] Inst,
  output [5:0] Opcode,
  output [4:0] Reg1,
  output [4:0] Reg2,
  output [4:0] Destino,
  output [4:0] Shift,
  output [5:0] Funct,
  output [15:0] Imm_Val,
  output [25:0] addr
);


  assign addr = Inst[25:0];
  assign Destino = Inst[15:11];
  assign Funct = Inst[5:0];
  assign Imm_Val = Inst[15:0];
  assign Opcode = Inst[31:26];
  assign Reg1 = Inst[25:21];
  assign Reg2 = Inst[20:16];
  assign Shift = Inst[10:6];
endmodule

module Interpreter_OPCOde (
  input  [5:0] Opcode,
  output Tipo_I,
  output Tipo_J,
  output Tipo_R
);

  wire not_1_out, not_2_out, not_3_out, not_4_out, not_5_out, not_6_out, not_7_out, not_8_out, not_9_out,
       not_10_out, not_11_out, not_12_out, not_13_out, not_14_out, not_15_out, not_16_out;

  not not_1 (not_1_out, Opcode[5]);
  not not_2 (not_2_out, Opcode[4]);
  not not_3 (not_3_out, Opcode[2]);
  not not_4 (not_4_out, Opcode[1]);
  not not_5 (not_5_out, Opcode[0]);
  not not_6 (not_6_out, Opcode[5]);
  not not_7 (not_7_out, Opcode[4]);
  not not_8 (not_8_out, Opcode[3]);
  not not_9 (not_9_out, Opcode[2]);
  not not_10 (not_10_out, Opcode[0]);
  not not_11 (not_11_out, Opcode[5]);
  not not_12 (not_12_out, Opcode[4]);
  not not_13 (not_13_out, Opcode[3]);
  not not_14 (not_14_out, Opcode[2]);
  not not_15 (not_15_out, Opcode[1]);
  not not_16 (not_16_out, Opcode[0]);
  and and_1 (Tipo_I, not_1_out, not_2_out, Opcode[3], not_3_out, not_4_out, not_5_out);
  and and_2 (Tipo_J, not_6_out, not_7_out, not_8_out, not_9_out, Opcode[1], not_10_out);
  and and_3 (Tipo_R, not_11_out, not_12_out, not_13_out, not_14_out, not_15_out, not_16_out);
endmodule
